# Fritzing sketch TinyDimmer (saved by Fritzing 0.9.4)
perfboards: 1

parts:
  U1 = attiny85 [package=dip]
  J1 = female pin header, 6 pins [form="♀ (female)"]
  J3 = female pin header, 1 pin [form="♀ (female)"]
  J4 = female pin header, 3 pins [form="♀ (female)"]
  J5 = female pin header, 1 pin [form="♀ (female)"]
  S1 = Pushbutton [package="[SMD]"]
  U2 = POT [package=pot_alpha_rv16af-20]
  R1 = Resistor [tolerance=±5% resistance=1k package="0805 [SMD]"]
  J2 = female pin header, 1 pin [form="♀ (female)"]
  J6 = female pin header, 1 pin [form="♀ (female)"]
  C1 = Capacitor Polarized [package=panasonic_c]  # not connected

nets:
  N1: U1.Pin_1, J1.pin1
  N2: U1.Pin_3, J3.pin1, U2.S
  N3: U1.Pin_5, J1.pin3
  N4: U1.Pin_6, J1.pin4
  N5: U1.Pin_7, J1.pin5, J5.pin1, S1.Pin_3, S1.Pin_4
  N6: J1.pin2, J4.pin3
  N7: J1.pin6, R1.Pin_0, J2.pin1
  N8: J4.pin1, U2.E
  N9: J4.pin2, S1.Pin_2
  N10: U2.A, R1.Pin_1, J6.pin1

notes:
  Yellow - RESET
  Black - GND
  Cyan - MOSI
  Green - MISO
  Orange - SCK
  Red - VCC
  WS2812
  Black - GND
  Green - DIN
  Red - 5V Vcc
  GND
  5V VCC
